// Logisim project hw2_khavar_jabbarli.circ as structural Verilog: 1 circuit, main circuit main
module main (
);

  wire a_XOR_X_out, ac_prime_bx_out, and_1_out, ax___bcx_prime_out, ax_out, bcx_prime_out, c_x_prime_out,
       clock_1_out, not_1_out, not_2_out, not_3_out, not_4_out, or_2_out, or_3_out, OR_out,
       x_a_prime___b_prime_out, x_prime_c_out, x_prime_c_xb_out, xb_out, xc_prime_out, xcb_prime_out,
       xnor_1_out, xnor_2_out, xnor_3_out;
  wire [2:0] j_k_ff_1_q, t_ff_4_q;

  not not_1 (not_1_out, j_k_ff_1_q[0]);
  not not_2 (not_2_out, j_k_ff_1_q[1]);
  Clock clock_1 (.out(clock_1_out));
  xor a_XOR_X (a_XOR_X_out, j_k_ff_1_q[2], and_1_out);
  and xc_prime (xc_prime_out, and_1_out, not_1_out);
  not not_3 (not_3_out, j_k_ff_1_q[2]);
  or OR (OR_out, a_XOR_X_out, xc_prime_out);
  and ac_prime_bx (ac_prime_bx_out, xc_prime_out, j_k_ff_1_q[2], j_k_ff_1_q[1]);
  and xcb_prime (xcb_prime_out, j_k_ff_1_q[0], and_1_out, not_2_out);
  or or_2 (or_2_out, not_2_out, not_3_out);
  or or_3 (or_3_out, ac_prime_bx_out, xcb_prime_out);
  and x_a_prime___b_prime (x_a_prime___b_prime_out, or_2_out, and_1_out);
  not not_4 (not_4_out, and_1_out);
  D_Flip_Flop d_ff_1 (.clk(clock_1_out), .D(OR_out), .Q(j_k_ff_1_q[2]));  // open: Qn, preset, en, reset
  T_Flip_Flop t_ff_1 (.clk(clock_1_out), .T(or_3_out), .Q(j_k_ff_1_q[1]));  // open: Qn, preset, reset, en
  J_K_Flip_Flop j_k_ff_1 (
    .J(x_a_prime___b_prime_out), .clk(clock_1_out), .K(x_a_prime___b_prime_out), .Q(j_k_ff_1_q[0]));  // open: Qn, preset, en, reset
  and ax (ax_out, t_ff_4_q[2], and_1_out);
  and bcx_prime (bcx_prime_out, t_ff_4_q[1], t_ff_4_q[0], not_4_out);
  and x_prime_c (x_prime_c_out, not_4_out, t_ff_4_q[0]);
  and xb (xb_out, and_1_out, t_ff_4_q[1]);
  or ax___bcx_prime (ax___bcx_prime_out, ax_out, bcx_prime_out);
  or x_prime_c_xb (x_prime_c_xb_out, x_prime_c_out, xb_out);
  or c_x_prime (c_x_prime_out, t_ff_4_q[0], not_4_out);
  T_Flip_Flop t_ff_2 (.clk(clock_1_out), .T(ax___bcx_prime_out), .Q(t_ff_4_q[2]));  // open: Qn, preset, reset, en
  T_Flip_Flop t_ff_3 (.clk(clock_1_out), .T(x_prime_c_xb_out), .Q(t_ff_4_q[1]));  // open: Qn, preset, reset, en
  T_Flip_Flop t_ff_4 (.clk(clock_1_out), .T(c_x_prime_out), .Q(t_ff_4_q[0]));  // open: Qn, preset, reset, en
  xnor xnor_1 (xnor_1_out, j_k_ff_1_q[2], t_ff_4_q[2]);
  xnor xnor_2 (xnor_2_out, j_k_ff_1_q[1], t_ff_4_q[1]);
  xnor xnor_3 (xnor_3_out, j_k_ff_1_q[0], t_ff_4_q[0]);
  and and_1 (and_1_out, xnor_1_out, xnor_2_out, xnor_3_out);
  Hex_Digit_Display hex_digit_display_1 (.value({1'b0, j_k_ff_1_q}));  // open: dp
  Hex_Digit_Display hex_digit_display_2 (.value({1'b0, t_ff_4_q}));  // open: dp

  // Notes on the sheet:
  //   a
  //   x
  //   a
  //   c
  //   c'
  //   x
  //   b
  //   b
  //   b'
  //   a'
  //   a' + b'
  //   x
  //   (a XOR x) + xc'
  //   xcb' + abc'x
  //   a
  //   x
  //   b
  //   c
  //   x
  //   b
  //   x'
  //   A(next)
  //   B(next)
  //   C(next)
  //   x'
  //   x
  //   c
  //   b
  //   c
  //   x'
  //   A(next)
  //   B(next)
  //   C(next)
endmodule
